# Fritzing sketch spires (saved by Fritzing 1.0.3b)
circuit board: 8.79cm x 6.5cm
breadboards: 2

parts:
  10k = Rotary Potentiometer (Small) [maximum_resistance=100kΩ knob_status=50% power=0.5W package=THT]
  S3 = Pushbutton [package="[THT]"]
  S2 = Pushbutton [package="[THT]"]
  JGND = female pin header, 4 pins [form="♀ (female)"]
  J+ = female pin header, 4 pins [form="♀ (female)"]
  1K = Resistor [tolerance=±5% resistance=4.7k power=0.25W package=THT]
  1K_2 = Resistor [tolerance=±5% resistance=1k power=0.25W package=THT]
  1k = Resistor [tolerance=±5% resistance=1k power=0.25W package=THT]
  1k_2 = Resistor [tolerance=±5% resistance=1k power=0.25W package=THT]
  JAIN = female pin header, 2 pins [form="♀ (female)"]
  LED1 = LED - 3mm [color="Red (633nm)" current=0.030A package="3 mm [THT]"]
  4_7k = Resistor [tolerance=±5% resistance=4.7k power=0.25W package=THT]
  Nano = Arduino Nano (Rev3.0)
  104 = Capacitor [package=cap-pth-5mm]
  105 = Capacitor [package=cap-pth-5mm]
  10K2 = Rotary Potentiometer (Small) [maximum_resistance=10kΩ knob_status=50% power=0.5W package=THT]
  100Ω1 = Resistor [tolerance=±5% power=0.25 resistance=100 package=THT]
  10K3 = Resistor [tolerance=±5% power=0.25 resistance=10k package=THT]
  100Ω2 = Resistor [tolerance=±5% power=0.25 resistance=100 package=THT]
  Audio_OUt1 = Audio Jack (TRS) 3.5mm [package="PG203J [THT]"]
  clckaudio1 = Audio Jack (TRS) 3.5mm [package="PG203J [THT]"]
  1KΩ1 = Resistor [tolerance=±5% resistance=1k power=0.25W package=THT]
  RE1 = Rotary Encoder [package=THT]
  VCC1 = 4 x AAA Battery Mount [internal_resistance=0.1Ω]
  S5 = SPST Switch [package=switch-spdt_kit]
  J8/7 = female pin header, 2 pins [form="♀ (female)"]
  RXTX = female pin header, 2 pins [form="♀ (female)"]
  J13 = female pin header, 5 pins [form="♀ (female)"]

nets:
  GND: 10k.leg1, S3.Pin_1, S3.Pin_2, S2.Pin_1, S2.Pin_2, 1K.Pin_1, 1K_2.Pin_1, 1k.Pin_1, 1k_2.Pin_1, JAIN.pin1, 4_7k.Pin_1, Nano.GND, 104.1, 10K3.Pin_1, Audio_OUt1.Sleeve, clckaudio1.Sleeve, RE1.GND, RE1.SW-2, VCC1.-, J13.pin2
  N1: 10k.wiper, Nano.A0
  V++: 10k.leg2, J+.pin1, J+.pin2, J+.pin3, J+.pin4, Nano.5V, J13.pin1
  N2: S3.Pin_3, S3.Pin_4, Nano.D3, J13.pin5
  N3: S2.Pin_3, S2.Pin_4, Nano.D2, J13.pin4
  N4: JGND.pin1, 1K.Pin_0
  N5: JGND.pin2, 1K_2.Pin_0
  N6: JGND.pin3, 1k.Pin_0
  N7: JGND.pin4, 1k_2.Pin_0
  N8: JAIN.pin2, 10K2.leg1
  N9: LED1.cathode, 4_7k.Pin_0
  N10: LED1.anode, Nano.D13/SCK
  N11: Nano.D1/TX, 1KΩ1.Pin_0, RXTX.pin2
  N12: Nano.D0/RX, RXTX.pin1
  N13: Nano.D4, RE1.SW-1
  N14: Nano.D5, RE1.Pin-B
  N15: Nano.D6, RE1.Pin-A
  N16: Nano.D7, J8/7.pin2
  N17: Nano.D8, J8/7.pin1
  N18: Nano.VIN, S5.S
  N19: 104.2, 10K2.leg2, 100Ω1.Pin_1
  N20: 105.2, 10K3.Pin_0, 100Ω2.Pin_1
  N21: 10K2.wiper, 100Ω2.Pin_0
  N22: 100Ω1.Pin_0, Audio_OUt1.Ring, Audio_OUt1.Tip, clckaudio1.Ring
  N23: clckaudio1.Tip, 1KΩ1.Pin_1
  N24: VCC1.+, S5.P

notes:
  spires v1
  blueprint@poetaster.de 2024

custom parts:
  Rotary Encoder: Rotary Encoder with push button
